# Fritzing sketch main (saved by Fritzing 0.9.3b)
breadboards: 3

parts:
  パーツ1 = Arduino Uno (Rev3)
  LCD1 = LCD screen  # not connected
  S1 = Pushbutton [package="[THT]"]
  R1 = Trimmer Potentiometer [maximum_resistance=10kΩ package=THT]
  S2 = Pushbutton [package="[THT]"]
  S3 = Pushbutton [package="[THT]"]
  R2 = Resistor [tolerance=±5% resistance=220 package=THT]
  R3 = Resistor [tolerance=±5% resistance=220 package=THT]
  R4 = Resistor [tolerance=±5% resistance=220 package=THT]

nets:
  N1: パーツ1.D5_PWM, S1.Pin_1, S1.Pin_2, R4.Pin_1
  N2: パーツ1.D6_PWM, S2.Pin_1, S2.Pin_2, R3.Pin_1
  N3: パーツ1.D7, S3.Pin_1, S3.Pin_2, R2.Pin_1
  N4: パーツ1.5V, R1.leg1, R2.Pin_0, R3.Pin_0, R4.Pin_0
  N5: パーツ1.GND, S1.Pin_3, S1.Pin_4, R1.leg2, S2.Pin_3, S2.Pin_4, S3.Pin_3, S3.Pin_4
